# Fritzing sketch farm_coop (saved by Fritzing 0.9.1b)
breadboards: 1

parts:
  Part1 = Photon
  Part2 = Breakout Board for Electret Microphone

nets (from the schematic view):
  N1: Part1.DAC, Part2.AUD
  GND: Part1.GND, Part2.GND
  3V3: Part1.3V3, Part2.VCC
